// Logisim project LogismDesign.circ as structural Verilog: 22 circuits, main circuit Register File
module main (
  output [17:0] out_1,
  output [17:0] out_2,
  output [17:0] out_3,
  output [17:0] out_4,
  output [17:0] out_5,
  output [17:0] out_6,
  output [17:0] out_7,
  output [17:0] out_8,
  output [17:0] out_9,
  output [17:0] out_10,
  output [17:0] out_11,
  output [17:0] out_12,
  output [17:0] out_13,
  output [17:0] out_14,
  output [17:0] out_15,
  output [17:0] out_16
);

  wire b_operator_1_b_out, clock_1_out, control_unit_1_aluoperanddecider, control_unit_1_ld2,
       control_unit_1_memoryload, control_unit_1_pcwrite, control_unit_1_registerload, control_unit_1_st,
       PCSet;
  wire [1:0] control_unit_1_alucontrol, control_unit_1_pcaddressdecider;
  wire [3:0] control_unit_1_rd1, control_unit_1_rd2, control_unit_1_wr;
  wire [9:0] MemAdrr;
  wire [17:0] _2_0__Z_Extent_out_2, _5_0__S_Extent_out_2, _13_0__S_Extent_out_2, alu_1_aluout,
       multiplexer_1_out, multiplexer_2_out, multiplexer_3_out, multiplexer_4_out, n18_bit_adder_1_sum,
       pc_1_outadress, ram_1_data, register_file_1_outdata1, register_file_1_outdata2;
  wire [17:10] rom_1_data;

  Clock clock_1 (.out(clock_1_out));
  PC pc_1 (
    .Clk(clock_1_out), .PCWrite(control_unit_1_pcwrite), .Setflag(PCSet), .inAddress(multiplexer_3_out),
    .outAdress(pc_1_outadress));
  ROM #(.addrWidth(18), .dataWidth(18)) rom_1 (.addr(pc_1_outadress), .data({rom_1_data, MemAdrr}), .sel(1'b1));
  Control_Unit control_unit_1 (
    .CU_Input({rom_1_data, MemAdrr}), .Clk(clock_1_out), .PCWrite(control_unit_1_pcwrite),
    .ALUOperandDecider(control_unit_1_aluoperanddecider), .ALUControl(control_unit_1_alucontrol),
    .RegisterLoad(control_unit_1_registerload), .PCAddressDecider(control_unit_1_pcaddressdecider),
    .memoryLoad(control_unit_1_memoryload), .ST(control_unit_1_st), .LD2(control_unit_1_ld2), .PCSet(PCSet),
    .Wr(control_unit_1_wr), .rd1(control_unit_1_rd1), .rd2(control_unit_1_rd2));
  Register_File register_file_1 (
    .Load(control_unit_1_registerload), .InData(multiplexer_4_out), .Clk(clock_1_out),
    .WR(control_unit_1_wr), .outData1(register_file_1_outdata1), .outData2(register_file_1_outdata2),
    .rd2(control_unit_1_rd2), .rd1(control_unit_1_rd1), .R0(out_1), .R1(out_2), .R2(out_3), .R3(out_4),
    .R4(out_5), .R5(out_6), .R6(out_7), .R7(out_8), .R8(out_9), .R9(out_10), .R10(out_11), .R11(out_12),
    .R12(out_13), .R13(out_14), .R14(out_15), .R15(out_16));
  _5_0__Sign_Extender _5_0__S_Extent (.in_1({rom_1_data, MemAdrr}), .out_2(_5_0__S_Extent_out_2));
  _13_0__Sign_Extender _13_0__S_Extent (.in_1({rom_1_data, MemAdrr}), .out_2(_13_0__S_Extent_out_2));
  _2_0__Zero_Extender _2_0__Z_Extent (.in_1({rom_1_data, MemAdrr}), .out_2(_2_0__Z_Extent_out_2));
  _18_Bit_Adder u_18_bit_adder_1 (.a(pc_1_outadress), .b(18'h1), .sum(n18_bit_adder_1_sum));
  Multiplexer #(.width(18), .enable("false")) multiplexer_1 (
    .in0(n18_bit_adder_1_sum), .in1(_2_0__Z_Extent_out_2), .out(multiplexer_1_out), .sel(b_operator_1_b_out));
  Multiplexer #(.width(18), .enable("false")) multiplexer_2 (
    .in0(register_file_1_outdata2), .in1(_5_0__S_Extent_out_2), .out(multiplexer_2_out),
    .sel(control_unit_1_aluoperanddecider));
  Multiplexer #(.select(2), .width(18), .enable("false")) multiplexer_3 (
    .in0(18'h1), .in1(_13_0__S_Extent_out_2), .in2(multiplexer_1_out), .in3(multiplexer_1_out),
    .out(multiplexer_3_out), .sel(control_unit_1_pcaddressdecider));
  ALU alu_1 (
    .Input1(register_file_1_outdata1), .Alucontrol(control_unit_1_alucontrol), .Aluout(alu_1_aluout),
    .Input2(multiplexer_2_out));
  B_Operator b_operator_1 (
    .op1(register_file_1_outdata1), .op2(register_file_1_outdata2), .B_out(b_operator_1_b_out),
    .nzpValue(MemAdrr[5:3]));
  RAM #(.addrWidth(10), .dataWidth(18), .bus("separate")) ram_1 (
    .addr(MemAdrr), .din(register_file_1_outdata1), .data(ram_1_data), .str(control_unit_1_st), .sel(1'b1),
    .clk(clock_1_out), .ld(control_unit_1_memoryload));  // open: clr
  Multiplexer #(.width(18), .enable("false")) multiplexer_4 (
    .in0(ram_1_data), .in1(alu_1_aluout), .out(multiplexer_4_out), .sel(control_unit_1_ld2));

  // Other names for the same wires on the sheet: NZP[2:0] = MemAdrr[5:3]; r0[17:0] = out_1; r1[17:0] = out_2;
  //   r2[17:0] = out_3; r3[17:0] = out_4; r4[17:0] = out_5; r5[17:0] = out_6; r6[17:0] = out_7; r7[17:0] = out_8;
  //   r8[17:0] = out_9; r9[17:0] = out_10; r10[17:0] = out_11; r11[17:0] = out_12; r12[17:0] = out_13;
  //   r13[17:0] = out_14; r14[17:0] = out_15; r15[17:0] = out_16

  // Notes on the sheet:
  //   contents of rom_1 (hex, n*v repeats v):
  //   1c44a 1c88a 3958d 19454 1d54a 38492
  //   Addr
  //   Addr
  //   ALU Operand decider
  //   Addr Decider
  //   B
endmodule

module Register_File (
  input  Load,
  input  [17:0] InData,
  input  Clk,
  input  [3:0] rd1,
  input  [3:0] WR,
  input  [3:0] rd2,
  output [17:0] R0,
  output [17:0] R1,
  output [17:0] R2,
  output [17:0] R3,
  output [17:0] R4,
  output [17:0] R5,
  output [17:0] outData1,
  output [17:0] R6,
  output [17:0] R7,
  output [17:0] outData2,
  output [17:0] R8,
  output [17:0] R9,
  output [17:0] R10,
  output [17:0] R11,
  output [17:0] R12,
  output [17:0] R13,
  output [17:0] R14,
  output [17:0] R15
);

  wire and_1_out, and_2_out, and_3_out, and_4_out, and_5_out, and_6_out, and_7_out, and_8_out, and_9_out,
       and_10_out, and_11_out, and_12_out, and_13_out, and_14_out, and_15_out, and_16_out, decoder_1_out0,
       decoder_1_out1, decoder_1_out2, decoder_1_out3, decoder_1_out4, decoder_1_out5, decoder_1_out6,
       decoder_1_out7, decoder_1_out8, decoder_1_out9, decoder_1_out10, decoder_1_out11, decoder_1_out12,
       decoder_1_out13, decoder_1_out14, decoder_1_out15;

  Decoder #(.select(4), .enable("false")) decoder_1 (
    .out0(decoder_1_out0), .out1(decoder_1_out1), .out2(decoder_1_out2), .out3(decoder_1_out3),
    .out4(decoder_1_out4), .out5(decoder_1_out5), .out6(decoder_1_out6), .out7(decoder_1_out7),
    .out8(decoder_1_out8), .out9(decoder_1_out9), .out10(decoder_1_out10), .out11(decoder_1_out11),
    .out12(decoder_1_out12), .out13(decoder_1_out13), .out14(decoder_1_out14), .out15(decoder_1_out15),
    .sel(WR));
  and and_1 (and_1_out, Load, decoder_1_out0);
  and and_2 (and_2_out, Load, decoder_1_out1);
  and and_3 (and_3_out, Load, decoder_1_out2);
  and and_4 (and_4_out, Load, decoder_1_out3);
  and and_5 (and_5_out, Load, decoder_1_out4);
  and and_6 (and_6_out, Load, decoder_1_out5);
  and and_7 (and_7_out, Load, decoder_1_out6);
  and and_8 (and_8_out, Load, decoder_1_out7);
  Register #(.width(18)) u_R0 (.D(InData), .en(and_1_out), .Q(R0), .clk(Clk), .clr(1'b0));
  Register #(.width(18)) u_R1 (.D(InData), .en(and_2_out), .Q(R1), .clk(Clk), .clr(1'b0));
  Register #(.width(18)) u_R2 (.D(InData), .en(and_3_out), .Q(R2), .clk(Clk), .clr(1'b0));
  Register #(.width(18)) u_R3 (.D(InData), .en(and_4_out), .Q(R3), .clk(Clk), .clr(1'b0));
  Register #(.width(18)) u_R4 (.D(InData), .en(and_5_out), .Q(R4), .clk(Clk), .clr(1'b0));
  Register #(.width(18)) u_R5 (.D(InData), .en(and_6_out), .Q(R5), .clk(Clk), .clr(1'b0));
  Register #(.width(18)) u_R6 (.D(InData), .en(and_7_out), .Q(R6), .clk(Clk), .clr(1'b0));
  Register #(.width(18)) u_R7 (.D(InData), .en(and_8_out), .Q(R7), .clk(Clk), .clr(1'b0));
  and and_9 (and_9_out, Load, decoder_1_out8);
  and and_10 (and_10_out, Load, decoder_1_out9);
  and and_11 (and_11_out, Load, decoder_1_out10);
  and and_12 (and_12_out, Load, decoder_1_out11);
  and and_13 (and_13_out, Load, decoder_1_out12);
  and and_14 (and_14_out, Load, decoder_1_out13);
  and and_15 (and_15_out, Load, decoder_1_out14);
  and and_16 (and_16_out, Load, decoder_1_out15);
  Register #(.width(18)) u_R8 (.D(InData), .en(and_9_out), .Q(R8), .clk(Clk), .clr(1'b0));
  Register #(.width(18)) u_R9 (.D(InData), .en(and_10_out), .Q(R9), .clk(Clk), .clr(1'b0));
  Register #(.width(18)) u_R10 (.D(InData), .en(and_11_out), .Q(R10), .clk(Clk), .clr(1'b0));
  Register #(.width(18)) u_R11 (.D(InData), .en(and_12_out), .Q(R11), .clk(Clk), .clr(1'b0));
  Register #(.width(18)) u_R12 (.D(InData), .en(and_13_out), .Q(R12), .clk(Clk), .clr(1'b0));
  Register #(.width(18)) u_R13 (.D(InData), .en(and_14_out), .Q(R13), .clk(Clk), .clr(1'b0));
  Register #(.width(18)) u_R14 (.D(InData), .en(and_15_out), .Q(R14), .clk(Clk), .clr(1'b0));
  Register #(.width(18)) u_R15 (.D(InData), .en(and_16_out), .Q(R15), .clk(Clk), .clr(1'b0));
  Multiplexer #(.select(4), .width(18), .enable("false")) multiplexer_1 (
    .in0(R0), .in1(R1), .in2(R2), .in3(R3), .in4(R4), .in5(R5), .in6(R6), .in7(R7), .in8(R8), .in9(R9),
    .in10(R10), .in11(R11), .in12(R12), .in13(R13), .in14(R14), .in15(R15), .out(outData1), .sel(rd1));
  Multiplexer #(.select(4), .width(18), .enable("false")) multiplexer_2 (
    .in0(R0), .in1(R1), .in2(R2), .in3(R3), .in4(R4), .in5(R5), .in6(R6), .in7(R7), .in8(R8), .in9(R9),
    .in10(R10), .in11(R11), .in12(R12), .in13(R13), .in14(R14), .in15(R15), .out(outData2), .sel(rd2));
endmodule

module ALU (
  input  [17:0] Input1,
  input  [17:0] Input2,
  input  [1:0] Alucontrol,
  output [17:0] Aluout
);

  wire [17:0] and_1_out, n18_bit_adder_1_sum, or_1_out, xor_1_out;

  _18_Bit_Adder u_18_bit_adder_1 (.a(Input1), .b(Input2), .sum(n18_bit_adder_1_sum));
  assign and_1_out = Input1 & Input2;  // AND_Gate and_1, 18 bits wide
  assign or_1_out = Input1 | Input2;  // OR_Gate or_1, 18 bits wide
  assign xor_1_out = Input1 ^ Input2;  // XOR_Gate xor_1, 18 bits wide
  Multiplexer #(.select(2), .width(18), .enable("false")) multiplexer_1 (
    .in0(n18_bit_adder_1_sum), .in1(and_1_out), .in2(or_1_out), .in3(xor_1_out), .out(Aluout),
    .sel(Alucontrol));
endmodule

module PC (
  input  Clk,
  input  PCWrite,
  input  Setflag,
  input  [17:0] inAddress,
  output [17:0] outAdress
);

  wire [17:0] multiplexer_1_out, multiplexer_2_out, n18_bit_adder_1_sum, n18_bit_adder_2_sum,
       n18_bit_subtractor_1_difference, not_1_out;

  assign not_1_out = ~inAddress;  // NOT_Gate not_1, 18 bits wide
  Multiplexer #(.width(18), .enable("false")) multiplexer_1 (
    .in0(multiplexer_2_out), .in1(inAddress), .out(multiplexer_1_out), .sel(Setflag));
  _18_Bit_Adder u_18_bit_adder_1 (.a(not_1_out), .b(18'h1), .sum(n18_bit_adder_1_sum));
  Register #(.width(18)) register_1 (.D(multiplexer_1_out), .en(PCWrite), .Q(outAdress), .clk(Clk));  // open: clr
  _18_Bit_Adder u_18_bit_adder_2 (.a(outAdress), .b(inAddress), .sum(n18_bit_adder_2_sum));
  _18_Bit_Subtractor u_18_bit_subtractor_1 (
    .a(outAdress), .b(n18_bit_adder_1_sum), .difference(n18_bit_subtractor_1_difference));
  Multiplexer #(.width(18), .enable("false")) multiplexer_2 (
    .in0(n18_bit_adder_2_sum), .in1(n18_bit_subtractor_1_difference), .out(multiplexer_2_out),
    .sel(inAddress[17]));
endmodule

// Control unit
module Control_Unit (
  input  [17:0] CU_Input,
  input  Clk,
  output PCSet,
  output ST,
  output LD2,
  output memoryLoad,
  output [1:0] PCAddressDecider,
  output RegisterLoad,
  output [1:0] ALUControl,
  output ALUOperandDecider,
  output PCWrite,
  output [3:0] rd2,
  output [3:0] rd1,
  output [3:0] Wr
);

  wire ADD_out, and_1_out, AND_2_out, and_3_out, and_4_out, B_out, decoder_1_out0, decoder_1_out1,
       decoder_1_out2, decoder_1_out3, decoder_1_out4, decoder_1_out5, decoder_1_out6, decoder_1_out7,
       decoder_1_out8, decoder_1_out9, decoder_1_out10, decoder_1_out11, decoder_1_out12, not_1_out,
       not_2_out, not_3_out, not_4_out, not_5_out, not_6_out, or_1_out, or_3_out, OR_4_out, register_1_q,
       ST_out, XOR_out;
  wire [3:0] counter_1_output;

  Counter counter_1 (
    .Data(CU_Input[17:14]), .Load(decoder_1_out1), .Count(or_1_out), .Output(counter_1_output),
    .Clear(and_1_out), .Clock(Clk));
  and and_1 (and_1_out, not_1_out, register_1_q);
  not not_1 (not_1_out, or_1_out);
  Register #(.width(1)) register_1 (.D(PCWrite), .en(1'b1), .Q(register_1_q), .clk(Clk), .clr(1'b0));
  Decoder #(.select(4), .enable("false")) decoder_1 (
    .out0(decoder_1_out0), .out1(decoder_1_out1), .out2(decoder_1_out2), .out3(decoder_1_out3),
    .out4(decoder_1_out4), .out5(decoder_1_out5), .out6(decoder_1_out6), .out7(decoder_1_out7),
    .out8(decoder_1_out8), .out9(decoder_1_out9), .out10(decoder_1_out10), .out11(decoder_1_out11),
    .out12(decoder_1_out12), .out13(ST), .out14(PCSet), .sel(counter_1_output));  // open: out15
  or or_1 (or_1_out, decoder_1_out0, decoder_1_out11);
  not not_2 (not_2_out, CU_Input[15]);
  and u_ST (ST_out, CU_Input[14], not_2_out, CU_Input[16], CU_Input[17]);
  not not_3 (not_3_out, CU_Input[14]);
  and B (B_out, not_3_out, CU_Input[15], CU_Input[16], CU_Input[17]);
  or AND_2 (AND_2_out, decoder_1_out3, decoder_1_out2);
  or or_2 (PCWrite, PCSet, ST, decoder_1_out12, decoder_1_out10, decoder_1_out9, decoder_1_out8, decoder_1_out7, decoder_1_out6, decoder_1_out5, decoder_1_out4, decoder_1_out3, decoder_1_out2);
  or or_3 (or_3_out, ST_out, B_out);
  or XOR (XOR_out, decoder_1_out9, decoder_1_out8);
  or ADD (ADD_out, decoder_1_out7, decoder_1_out6);
  or OR_4 (OR_4_out, decoder_1_out5, decoder_1_out4);
  or or_5 (ALUOperandDecider, decoder_1_out9, decoder_1_out7, decoder_1_out5, decoder_1_out3);
  assign rd1 = or_3_out ? CU_Input[13:10] : 4'bz;  // Controlled_Buffer controlled_buffer_1
  not not_4 (not_4_out, or_3_out);
  assign rd1 = not_4_out ? CU_Input[9:6] : 4'bz;  // Controlled_Buffer controlled_buffer_2
  and and_3 (and_3_out, ADD_out, AND_2_out);
  and and_4 (and_4_out, ADD_out, OR_4_out);
  Multiplexer #(.width(4), .enable("false")) multiplexer_1 (
    .in0(CU_Input[9:6]), .in1(CU_Input[5:2]), .out(rd2), .sel(not_4_out));
  and and_5 (PCAddressDecider[0], decoder_1_out10, not_5_out);
  not not_5 (not_5_out, PCSet);
  and and_6 (PCAddressDecider[1], PCSet, not_6_out);
  not not_6 (not_6_out, decoder_1_out10);
  or or_6 (RegisterLoad, decoder_1_out12, decoder_1_out9, decoder_1_out8, decoder_1_out7, decoder_1_out6, decoder_1_out5, decoder_1_out4, decoder_1_out3, decoder_1_out2);
  or _1 (ALUControl[1], XOR_out, and_3_out, OR_4_out);
  or _0 (ALUControl[0], XOR_out, and_4_out, AND_2_out);
  not not_7 (LD2, decoder_1_out12);
  or or_7 (memoryLoad, decoder_1_out12, decoder_1_out11);

  assign Wr = CU_Input[13:10];

  // Notes on the sheet:
  //   Fetch1
  //   Fetch2
  //   AND1
  //   ANDI1
  //   OR1
  //   ORI1
  //   ADD1
  //   ADDI1
  //   XOR1
  //   XORI1
  //   JUMP1
  //   LD1
  //   LD2
  //   ST1
  //   B1
endmodule

module _6_18_Extender (
  input  [5:0] inputImm,
  output [17:0] OutputImm
);

  assign OutputImm = {{12{inputImm[5]}}, inputImm};  // Bit_Extender bit_extender_1
endmodule

// Imm
module _5_0__Sign_Extender (
  input  [17:0] in_1,
  output [17:0] out_2
);

  assign out_2 = {{12{in_1[5]}}, in_1[5:0]};  // Bit_Extender bit_extender_1
endmodule

// HA
module Half_Adder (
  input  a,
  input  b,
  output S,
  output Cout
);

  xor xor_1 (S, a, b);
  and and_1 (Cout, a, b);
endmodule

// Jump
module _13_0__Sign_Extender (
  input  [17:0] in_1,
  output [17:0] out_2
);

  assign out_2 = {{4{in_1[13]}}, in_1[13:0]};  // Bit_Extender bit_extender_1
endmodule

// LD1
module _9_0__0_Extender (
  input  [17:0] in_1,
  output [17:0] out_2
);

  assign out_2 = {{8{1'b0}}, in_1[9:0]};  // Bit_Extender bit_extender_1
endmodule

// B
module _2_0__Zero_Extender (
  input  [17:0] in_1,
  output [17:0] out_2
);

  assign out_2 = {{15{1'b0}}, in_1[2:0]};  // Bit_Extender bit_extender_1
endmodule

// FA
module Full_Adder (
  input  a,
  input  b,
  input  Cin,
  output S,
  output Cout
);

  wire and_1_out, and_2_out, and_3_out;

  and and_1 (and_1_out, a, Cin);
  and and_2 (and_2_out, b, Cin);
  and and_3 (and_3_out, b, a);
  xor xor_1 (S, a, b, Cin);
  or or_1 (Cout, and_1_out, and_2_out, and_3_out);
endmodule

// Adder
module _18_Bit_Adder (
  input  [17:0] a,
  input  [17:0] b,
  output [17:0] sum
);

  wire full_adder_1_cout, full_adder_2_cout, full_adder_3_cout, full_adder_4_cout, full_adder_5_cout,
       full_adder_6_cout, full_adder_7_cout, full_adder_8_cout, full_adder_9_cout, full_adder_10_cout,
       full_adder_11_cout, full_adder_12_cout, full_adder_13_cout, full_adder_14_cout, full_adder_15_cout,
       full_adder_17_cout, half_adder_1_cout;

  Full_Adder full_adder_1 (.a(a[1]), .b(b[1]), .Cin(half_adder_1_cout), .S(sum[1]), .Cout(full_adder_1_cout));
  Half_Adder half_adder_1 (.a(a[0]), .b(b[0]), .S(sum[0]), .Cout(half_adder_1_cout));
  Full_Adder full_adder_2 (.a(a[2]), .b(b[2]), .Cin(full_adder_1_cout), .S(sum[2]), .Cout(full_adder_2_cout));
  Full_Adder full_adder_3 (.a(a[3]), .b(b[3]), .Cin(full_adder_2_cout), .S(sum[3]), .Cout(full_adder_3_cout));
  Full_Adder full_adder_4 (.a(a[4]), .b(b[4]), .Cin(full_adder_3_cout), .S(sum[4]), .Cout(full_adder_4_cout));
  Full_Adder full_adder_5 (.a(a[5]), .b(b[5]), .Cin(full_adder_4_cout), .S(sum[5]), .Cout(full_adder_5_cout));
  Full_Adder full_adder_6 (.a(a[6]), .b(b[6]), .Cin(full_adder_5_cout), .S(sum[6]), .Cout(full_adder_6_cout));
  Full_Adder full_adder_7 (.a(a[7]), .b(b[7]), .Cin(full_adder_6_cout), .S(sum[7]), .Cout(full_adder_7_cout));
  Full_Adder full_adder_8 (.a(a[9]), .b(b[9]), .Cin(full_adder_9_cout), .S(sum[9]), .Cout(full_adder_8_cout));
  Full_Adder full_adder_9 (.a(a[8]), .b(b[8]), .Cin(full_adder_7_cout), .S(sum[8]), .Cout(full_adder_9_cout));
  Full_Adder full_adder_10 (.a(a[10]), .b(b[10]), .Cin(full_adder_8_cout), .S(sum[10]), .Cout(full_adder_10_cout));
  Full_Adder full_adder_11 (.a(a[11]), .b(b[11]), .Cin(full_adder_10_cout), .S(sum[11]), .Cout(full_adder_11_cout));
  Full_Adder full_adder_12 (.a(a[12]), .b(b[12]), .Cin(full_adder_11_cout), .S(sum[12]), .Cout(full_adder_12_cout));
  Full_Adder full_adder_13 (.a(a[13]), .b(b[13]), .Cin(full_adder_12_cout), .S(sum[13]), .Cout(full_adder_13_cout));
  Full_Adder full_adder_14 (.a(a[14]), .b(b[14]), .Cin(full_adder_13_cout), .S(sum[14]), .Cout(full_adder_14_cout));
  Full_Adder full_adder_15 (.a(a[15]), .b(b[15]), .Cin(full_adder_14_cout), .S(sum[15]), .Cout(full_adder_15_cout));
  Full_Adder full_adder_16 (.a(a[17]), .b(b[17]), .Cin(full_adder_17_cout), .S(sum[17]));  // open: Cout
  Full_Adder full_adder_17 (.a(a[16]), .b(b[16]), .Cin(full_adder_15_cout), .S(sum[16]), .Cout(full_adder_17_cout));
endmodule

// Operator
module B_Operator (
  input  [2:0] nzpValue,
  input  [17:0] op1,
  input  [17:0] op2,
  output B_out
);

  wire BEQ, BGE, BGT, BLE, BLT;

  _18_Bit_Comparator _18_Bit_Comparator (.a(op1), .b(op2), .gt(BGT), .eq(BEQ), .lt(BLT));
  or or_1 (BLE, BEQ, BLT);
  or or_2 (BGE, BEQ, BGT);
  Multiplexer #(.select(3), .enable("false")) multiplexer_1 (
    .in1(BGT), .in2(BEQ), .in3(BGE), .in4(BLT), .in6(BLE), .out(B_out), .sel(nzpValue));  // open: in0, in5, in7
endmodule

// HC
module Half_Comparator (
  input  a,
  input  b,
  output gt,
  output eq,
  output lt
);

  wire not_1_out, not_2_out;

  not not_1 (not_1_out, b);
  not not_2 (not_2_out, a);
  and and_1 (gt, a, not_1_out);
  xnor xnor_1 (eq, a, b);
  and and_2 (lt, not_2_out, b);
endmodule

// FC
module Full_Comparator (
  input  a,
  input  b,
  input  gtin,
  input  eqin,
  input  ltin,
  output gt,
  output eq,
  output lt
);

  wire and_1_out, and_2_out, not_1_out, not_2_out, xnor_1_out;

  not not_1 (not_1_out, a);
  and and_1 (and_1_out, a, eqin, not_2_out);
  not not_2 (not_2_out, b);
  xnor xnor_1 (xnor_1_out, a, b);
  and and_2 (and_2_out, not_1_out, b, eqin);
  or or_1 (gt, and_1_out, gtin);
  and and_3 (eq, eqin, xnor_1_out);
  or or_2 (lt, ltin, and_2_out);
endmodule

module _18_Bit_Comparator (
  input  [17:0] a,
  input  [17:0] b,
  output gt,
  output eq,
  output lt
);

  wire full_comparator_1_eq, full_comparator_1_gt, full_comparator_1_lt, full_comparator_2_eq,
       full_comparator_2_gt, full_comparator_2_lt, full_comparator_3_eq, full_comparator_3_gt,
       full_comparator_3_lt, full_comparator_4_eq, full_comparator_4_gt, full_comparator_4_lt,
       full_comparator_5_eq, full_comparator_5_gt, full_comparator_5_lt, full_comparator_6_eq,
       full_comparator_6_gt, full_comparator_6_lt, full_comparator_7_eq, full_comparator_7_gt,
       full_comparator_7_lt, full_comparator_8_eq, full_comparator_8_gt, full_comparator_8_lt,
       full_comparator_9_eq, full_comparator_9_gt, full_comparator_9_lt, full_comparator_10_eq,
       full_comparator_10_gt, full_comparator_10_lt, full_comparator_11_eq, full_comparator_11_gt,
       full_comparator_11_lt, full_comparator_12_eq, full_comparator_12_gt, full_comparator_12_lt,
       full_comparator_13_eq, full_comparator_13_gt, full_comparator_13_lt, full_comparator_14_eq,
       full_comparator_14_gt, full_comparator_14_lt, full_comparator_15_eq, full_comparator_15_gt,
       full_comparator_15_lt, full_comparator_16_eq, full_comparator_16_gt, full_comparator_16_lt,
       half_comparator_1_eq, half_comparator_1_gt, half_comparator_1_lt;

  Half_Comparator half_comparator_1 (
    .a(a[17]), .b(b[17]), .gt(half_comparator_1_gt), .eq(half_comparator_1_eq), .lt(half_comparator_1_lt));
  Full_Comparator full_comparator_1 (
    .a(a[15]), .b(b[15]), .gtin(full_comparator_2_gt), .eqin(full_comparator_2_eq),
    .ltin(full_comparator_2_lt), .gt(full_comparator_1_gt), .eq(full_comparator_1_eq),
    .lt(full_comparator_1_lt));
  Full_Comparator full_comparator_2 (
    .a(a[16]), .b(b[16]), .gtin(half_comparator_1_gt), .eqin(half_comparator_1_eq),
    .ltin(half_comparator_1_lt), .gt(full_comparator_2_gt), .eq(full_comparator_2_eq),
    .lt(full_comparator_2_lt));
  Full_Comparator full_comparator_3 (
    .a(a[14]), .b(b[14]), .gtin(full_comparator_1_gt), .eqin(full_comparator_1_eq),
    .ltin(full_comparator_1_lt), .gt(full_comparator_3_gt), .eq(full_comparator_3_eq),
    .lt(full_comparator_3_lt));
  Full_Comparator full_comparator_4 (
    .a(a[13]), .b(b[13]), .gtin(full_comparator_3_gt), .eqin(full_comparator_3_eq),
    .ltin(full_comparator_3_lt), .gt(full_comparator_4_gt), .eq(full_comparator_4_eq),
    .lt(full_comparator_4_lt));
  Full_Comparator full_comparator_5 (
    .a(a[12]), .b(b[12]), .gtin(full_comparator_4_gt), .eqin(full_comparator_4_eq),
    .ltin(full_comparator_4_lt), .gt(full_comparator_5_gt), .eq(full_comparator_5_eq),
    .lt(full_comparator_5_lt));
  Full_Comparator full_comparator_6 (
    .a(a[11]), .b(b[11]), .gtin(full_comparator_5_gt), .eqin(full_comparator_5_eq),
    .ltin(full_comparator_5_lt), .gt(full_comparator_6_gt), .eq(full_comparator_6_eq),
    .lt(full_comparator_6_lt));
  Full_Comparator full_comparator_7 (
    .a(a[10]), .b(b[10]), .gtin(full_comparator_6_gt), .eqin(full_comparator_6_eq),
    .ltin(full_comparator_6_lt), .gt(full_comparator_7_gt), .eq(full_comparator_7_eq),
    .lt(full_comparator_7_lt));
  Full_Comparator full_comparator_8 (
    .a(a[9]), .b(b[9]), .gtin(full_comparator_7_gt), .eqin(full_comparator_7_eq),
    .ltin(full_comparator_7_lt), .gt(full_comparator_8_gt), .eq(full_comparator_8_eq),
    .lt(full_comparator_8_lt));
  Full_Comparator full_comparator_9 (
    .a(a[7]), .b(b[7]), .gtin(full_comparator_10_gt), .eqin(full_comparator_10_eq),
    .ltin(full_comparator_10_lt), .gt(full_comparator_9_gt), .eq(full_comparator_9_eq),
    .lt(full_comparator_9_lt));
  Full_Comparator full_comparator_10 (
    .a(a[8]), .b(b[8]), .gtin(full_comparator_8_gt), .eqin(full_comparator_8_eq),
    .ltin(full_comparator_8_lt), .gt(full_comparator_10_gt), .eq(full_comparator_10_eq),
    .lt(full_comparator_10_lt));
  Full_Comparator full_comparator_11 (
    .a(a[6]), .b(b[6]), .gtin(full_comparator_9_gt), .eqin(full_comparator_9_eq),
    .ltin(full_comparator_9_lt), .gt(full_comparator_11_gt), .eq(full_comparator_11_eq),
    .lt(full_comparator_11_lt));
  Full_Comparator full_comparator_12 (
    .a(a[5]), .b(b[5]), .gtin(full_comparator_11_gt), .eqin(full_comparator_11_eq),
    .ltin(full_comparator_11_lt), .gt(full_comparator_12_gt), .eq(full_comparator_12_eq),
    .lt(full_comparator_12_lt));
  Full_Comparator full_comparator_13 (
    .a(a[4]), .b(b[4]), .gtin(full_comparator_12_gt), .eqin(full_comparator_12_eq),
    .ltin(full_comparator_12_lt), .gt(full_comparator_13_gt), .eq(full_comparator_13_eq),
    .lt(full_comparator_13_lt));
  Full_Comparator full_comparator_14 (
    .a(a[3]), .b(b[3]), .gtin(full_comparator_13_gt), .eqin(full_comparator_13_eq),
    .ltin(full_comparator_13_lt), .gt(full_comparator_14_gt), .eq(full_comparator_14_eq),
    .lt(full_comparator_14_lt));
  Full_Comparator full_comparator_15 (
    .a(a[2]), .b(b[2]), .gtin(full_comparator_14_gt), .eqin(full_comparator_14_eq),
    .ltin(full_comparator_14_lt), .gt(full_comparator_15_gt), .eq(full_comparator_15_eq),
    .lt(full_comparator_15_lt));
  Full_Comparator full_comparator_16 (
    .a(a[1]), .b(b[1]), .gtin(full_comparator_15_gt), .eqin(full_comparator_15_eq),
    .ltin(full_comparator_15_lt), .gt(full_comparator_16_gt), .eq(full_comparator_16_eq),
    .lt(full_comparator_16_lt));
  Full_Comparator full_comparator_17 (
    .a(a[0]), .b(b[0]), .gtin(full_comparator_16_gt), .eqin(full_comparator_16_eq),
    .ltin(full_comparator_16_lt), .gt(gt), .eq(eq), .lt(lt));
endmodule

// Ctr
module Counter (
  input  [3:0] Data,
  input  Load,
  input  Count,
  input  Clock,
  input  Clear,
  output [3:0] Output
);

  wire [3:0] _4_Bit_Adder_out_3, multiplexer_1_out;

  Multiplexer #(.select(2), .width(4), .enable("false")) multiplexer_1 (
    .in0(Output), .in1(_4_Bit_Adder_out_3), .in2(Data), .out(multiplexer_1_out), .sel({Load, Count}));  // open: in3
  Register #(.width(4)) register_1 (.D(multiplexer_1_out), .Q(Output), .clk(Clock), .clr(Clear));  // open: en
  _4_Bit_Adder _4_Bit_Adder (.in_1(Output), .in_2(4'b0001), .out_3(_4_Bit_Adder_out_3));
endmodule

module Half_Subtractor (
  input  A,
  input  B,
  output Difference,
  output Borrow
);

  wire not_1_out;

  not not_1 (not_1_out, A);
  xor xor_1 (Difference, A, B);
  and and_1 (Borrow, not_1_out, B);
endmodule

module Full_Subtractor (
  input  A,
  input  B,
  input  Bin,
  output D,
  output Bout
);

  wire and_1_out, and_2_out, and_3_out, not_1_out;

  not not_1 (not_1_out, A);
  xor xor_1 (D, A, B, Bin);
  and and_1 (and_1_out, B, not_1_out);
  and and_2 (and_2_out, not_1_out, Bin);
  and and_3 (and_3_out, Bin, B);
  or or_1 (Bout, and_1_out, and_2_out, and_3_out);
endmodule

// Sub
module _18_Bit_Subtractor (
  input  [17:0] a,
  input  [17:0] b,
  output [17:0] difference
);

  wire full_subtractor_1_bout, full_subtractor_2_bout, full_subtractor_3_bout, full_subtractor_4_bout,
       full_subtractor_5_bout, full_subtractor_6_bout, full_subtractor_7_bout, full_subtractor_8_bout,
       full_subtractor_9_bout, full_subtractor_10_bout, full_subtractor_11_bout, full_subtractor_12_bout,
       full_subtractor_13_bout, full_subtractor_14_bout, full_subtractor_15_bout, full_subtractor_17_bout,
       half_subtractor_1_borrow;

  Full_Subtractor full_subtractor_1 (
    .A(a[1]), .B(b[1]), .Bin(half_subtractor_1_borrow), .D(difference[1]), .Bout(full_subtractor_1_bout));
  Half_Subtractor half_subtractor_1 (.A(a[0]), .B(b[0]), .Difference(difference[0]), .Borrow(half_subtractor_1_borrow));
  Full_Subtractor full_subtractor_2 (
    .A(a[2]), .B(b[2]), .Bin(full_subtractor_1_bout), .D(difference[2]), .Bout(full_subtractor_2_bout));
  Full_Subtractor full_subtractor_3 (
    .A(a[3]), .B(b[3]), .Bin(full_subtractor_2_bout), .D(difference[3]), .Bout(full_subtractor_3_bout));
  Full_Subtractor full_subtractor_4 (
    .A(a[5]), .B(b[5]), .Bin(full_subtractor_5_bout), .D(difference[5]), .Bout(full_subtractor_4_bout));
  Full_Subtractor full_subtractor_5 (
    .A(a[4]), .B(b[4]), .Bin(full_subtractor_3_bout), .D(difference[4]), .Bout(full_subtractor_5_bout));
  Full_Subtractor full_subtractor_6 (
    .A(a[6]), .B(b[6]), .Bin(full_subtractor_4_bout), .D(difference[6]), .Bout(full_subtractor_6_bout));
  Full_Subtractor full_subtractor_7 (
    .A(a[7]), .B(b[7]), .Bin(full_subtractor_6_bout), .D(difference[7]), .Bout(full_subtractor_7_bout));
  Full_Subtractor full_subtractor_8 (
    .A(a[9]), .B(b[9]), .Bin(full_subtractor_9_bout), .D(difference[9]), .Bout(full_subtractor_8_bout));
  Full_Subtractor full_subtractor_9 (
    .A(a[8]), .B(b[8]), .Bin(full_subtractor_7_bout), .D(difference[8]), .Bout(full_subtractor_9_bout));
  Full_Subtractor full_subtractor_10 (
    .A(a[10]), .B(b[10]), .Bin(full_subtractor_8_bout), .D(difference[10]), .Bout(full_subtractor_10_bout));
  Full_Subtractor full_subtractor_11 (
    .A(a[11]), .B(b[11]), .Bin(full_subtractor_10_bout), .D(difference[11]), .Bout(full_subtractor_11_bout));
  Full_Subtractor full_subtractor_12 (
    .A(a[13]), .B(b[13]), .Bin(full_subtractor_13_bout), .D(difference[13]), .Bout(full_subtractor_12_bout));
  Full_Subtractor full_subtractor_13 (
    .A(a[12]), .B(b[12]), .Bin(full_subtractor_11_bout), .D(difference[12]), .Bout(full_subtractor_13_bout));
  Full_Subtractor full_subtractor_14 (
    .A(a[14]), .B(b[14]), .Bin(full_subtractor_12_bout), .D(difference[14]), .Bout(full_subtractor_14_bout));
  Full_Subtractor full_subtractor_15 (
    .A(a[15]), .B(b[15]), .Bin(full_subtractor_14_bout), .D(difference[15]), .Bout(full_subtractor_15_bout));
  Full_Subtractor full_subtractor_16 (
    .A(a[17]), .B(b[17]), .Bin(full_subtractor_17_bout), .D(difference[17]));  // open: Bout
  Full_Subtractor full_subtractor_17 (
    .A(a[16]), .B(b[16]), .Bin(full_subtractor_15_bout), .D(difference[16]), .Bout(full_subtractor_17_bout));
endmodule

module _4_Bit_Adder (
  input  [3:0] in_1,
  input  [3:0] in_2,
  output [3:0] out_3
);

  wire full_adder_1_cout, full_adder_2_cout, half_adder_1_cout;

  Half_Adder half_adder_1 (.a(in_1[0]), .b(in_2[0]), .S(out_3[0]), .Cout(half_adder_1_cout));
  Full_Adder full_adder_1 (.a(in_1[1]), .b(in_2[1]), .Cin(half_adder_1_cout), .S(out_3[1]), .Cout(full_adder_1_cout));
  Full_Adder full_adder_2 (.a(in_1[2]), .b(in_2[2]), .Cin(full_adder_1_cout), .S(out_3[2]), .Cout(full_adder_2_cout));
  Full_Adder full_adder_3 (.a(in_1[3]), .b(in_2[3]), .Cin(full_adder_2_cout), .S(out_3[3]));  // open: Cout
endmodule
